# Fritzing sketch Automatic Gardening Sys (saved by Fritzing 0.9.3b)

parts:
  LCD_Screen = LCD-16X2 [package=lcd-16x2_noholes]
  Arduino_Mega = Arduino Mega 2560 (Rev3)
  Relay_module = RELAY [package=relay-jzc]
  Moisture_Sensor = Soil Moisture Sensor
  Temp_Sensor = Humidity and Temperature Sensor RHT03
  R1 = Resistor [tolerance=±5% resistance=220 package="0402 [SMD]"]
  R2 = 1kΩ Resistor [package="1206 [SMD]"]
  U2 = LIPO-2000mAh [package=lipo-2000]
  Solenoid_valve_to_pump_water = Solenoid
  VCC1 = Battery block 9V

nets:
  N1: LCD_Screen.VSS, R1.Pin_1
  VCC: LCD_Screen.VDD, Arduino_Mega.5V, Relay_module.COIL1, Moisture_Sensor.VCC, Temp_Sensor.Vcc
  N2: LCD_Screen.VO, Arduino_Mega.D1_TX0
  N3: LCD_Screen.RS, Arduino_Mega.D2_PWM
  N4: LCD_Screen.R_W, Arduino_Mega.D3_PWM
  N5: LCD_Screen.E, Arduino_Mega.D4_PWM
  N6: LCD_Screen.DB4, Arduino_Mega.D7_PWM
  N7: LCD_Screen.DB6, Arduino_Mega.D8_PWM
  N8: LCD_Screen.DB7, R2.Pin_1
  N9: LCD_Screen.K, R1.Pin_0
  N10: Arduino_Mega.A0, Moisture_Sensor.SIG
  N11: Arduino_Mega.A1, Temp_Sensor.Data-signal
  GND: Arduino_Mega.GND, Relay_module.MAIN, Moisture_Sensor.GND, Temp_Sensor.GND_1, R2.Pin_0, U2.-, Solenoid_valve_to_pump_water.pin1, VCC1.+
  N12: Arduino_Mega.D12_PWM, Relay_module.NO
  N13: Arduino_Mega.3V3, VCC1.-
  N14: Relay_module.NC, U2.+

notes:
  WATER LEVEL INDICATOR
  <Checks for water in supply container>

custom parts:
  1kΩ Resistor: A generic resistor
